// Logisim project brainfuck_machine.circ as structural Verilog: 2 circuits, main circuit main
module main (
  input  [7:0] EXT_INPUT,
  input  OUTPUT_READY,
  output [7:0] EXT_OUTPUT,
  output CLK
);

  wire and_1_out, and_2_out, and_3_out, and_4_out, and_5_out, and_6_out, and_7_out, and_8_out, and_9_out,
       and_10_out, and_11_out, and_12_out, and_13_out, and_14_out, and_15_out, and_16_out, clock_1_out,
       clock_2_out, clock_3_out, clock_4_out, clock_5_out, clock_6_out, clock_7_out, clock_8_out,
       clock_9_out, clock_10_out, clock_11_out, clock_12_out, clock_13_out, clock_14_out, clock_15_out,
       clock_16_out, comparator_1_eq, comparator_2_eq, comparator_3_eq, comparator_4_eq, comparator_5_eq,
       comparator_6_eq, comparator_8_eq, comparator_9_eq, comparator_10_eq, d_ff_1_q, d_ff_2_q, d_ff_3_q,
       d_ff_4_q, d_ff_5_q, monostable_1_pulse, monostable_2_pulse, monostable_3_pulse, monostable_4_pulse,
       nor_1_out, nor_2_out, not_1_out, not_2_out, not_3_out, not_4_out, not_5_out, not_6_out, not_7_out,
       not_8_out, not_9_out, or_1_out, or_2_out, or_3_out, or_4_out, RESET_out, STARTUP_qn;
  wire [0:0] comparator_7_eq, EXT_CLK_out;
  wire [7:0] adder_1_out, R_IN_q, R_OUT_q, ram_1_data, register_1_q, register_2_q, rom_1_data,
       subtractor_1_out;
  wire [14:0] counter_1_q, counter_2_q, counter_3_q, ram_2_data, undriven;

  Button RESET (.out(RESET_out));
  D_Flip_Flop STARTUP (.D(1'b1), .clk(clock_1_out), .Qn(STARTUP_qn), .reset(RESET_out));  // open: Q, preset
  Clock clock_1 (.out(clock_1_out));
  nor nor_1 (nor_1_out, comparator_1_eq, STARTUP_qn, d_ff_2_q, d_ff_4_q);
  nor nor_2 (nor_2_out, STARTUP_qn, d_ff_2_q, d_ff_4_q, d_ff_5_q);
  and and_1 (and_1_out, or_2_out, nor_2_out);
  Counter #(.max('h7fff), .width(15)) counter_1 (
    .clr(RESET_out), .load(and_7_out), .count(nor_1_out), .clk(clock_2_out), .D(ram_2_data), .Q(counter_1_q));  // open: up, carry
  Clock clock_2 (.out(clock_2_out));
  Counter #(.max('h7fff), .trigger("falling"), .width(15)) counter_2 (
    .clr(RESET_out), .up(comparator_2_eq), .count(and_1_out), .clk(clock_3_out), .D(undriven), .Q(counter_2_q));  // open: load, carry
  Clock clock_3 (.out(clock_3_out));
  Counter #(.max('h7fff), .trigger("falling"), .width(15)) counter_3 (
    .clr(RESET_out), .up(comparator_8_eq), .count(or_3_out), .clk(clock_4_out), .Q(counter_3_q));  // open: load, D, carry
  Clock clock_4 (.out(clock_4_out));
  Clock clock_5 (.out(clock_5_out));
  ROM #(.addrWidth(15)) rom_1 (.addr(counter_1_q), .data(rom_1_data));
  RAM #(.addrWidth(15), .asyncread("true"), .clearpin("true"), .databus("bidir"), .trigger("falling")) ram_1 (
    .addr(counter_2_q), .we(and_4_out), .oe(not_1_out), .clk(clock_5_out), .data(ram_1_data), .clr(RESET_out));
  not not_1 (not_1_out, and_4_out);
  not not_2 (not_2_out, and_16_out);
  Clock clock_6 (.out(clock_6_out));
  RAM #(.addrWidth(15), .asyncread("true"), .clearpin("true"), .dataWidth(15), .databus("bidir"), .trigger("falling")) ram_2 (
    .addr(counter_3_q), .we(and_16_out), .oe(not_2_out), .clk(clock_6_out), .data(ram_2_data), .clr(RESET_out));
  Adder adder_1 (.a(ram_1_data), .b(8'h1), .out(adder_1_out));  // open: cin, cout
  Subtractor subtractor_1 (.a(ram_1_data), .b(8'h1), .out(subtractor_1_out));  // open: bin, bout
  assign ram_2_data = and_16_out ? counter_1_q : 15'bz;  // Controlled_Buffer controlled_buffer_1
  Comparator comparator_1 (.a(rom_1_data), .b({8{1'b0}}), .eq(comparator_1_eq));  // open: gt, lt
  Comparator comparator_2 (.a(rom_1_data), .b(8'h3e), .eq(comparator_2_eq));  // open: gt, lt
  Comparator comparator_3 (.a(rom_1_data), .b(8'h3c), .eq(comparator_3_eq));  // open: gt, lt
  Comparator comparator_4 (.a(rom_1_data), .b(8'h2b), .eq(comparator_4_eq));  // open: gt, lt
  Comparator comparator_5 (.a(rom_1_data), .b(8'h2d), .eq(comparator_5_eq));  // open: gt, lt
  Comparator comparator_6 (.a(rom_1_data), .b(8'h2e), .eq(comparator_6_eq));  // open: gt, lt
  Comparator comparator_7 (.a(rom_1_data), .b(8'h2c), .eq(comparator_7_eq[0]));  // open: gt, lt
  Comparator comparator_8 (.a(rom_1_data), .b(8'h5b), .eq(comparator_8_eq));  // open: gt, lt
  Comparator comparator_9 (.a(rom_1_data), .b(8'h5d), .eq(comparator_9_eq));  // open: gt, lt
  not not_3 (not_3_out, d_ff_5_q);
  Register register_1 (.D(adder_1_out), .clk(clock_7_out), .Q(register_1_q));  // open: en, clr
  Clock clock_7 (.out(clock_7_out));
  Register register_2 (.D(subtractor_1_out), .clk(clock_8_out), .Q(register_2_q));  // open: en, clr
  Clock clock_8 (.out(clock_8_out));
  and and_2 (and_2_out, comparator_5_eq, not_3_out);
  and and_3 (and_3_out, comparator_4_eq, not_3_out);
  assign ram_1_data = and_3_out ? register_1_q : 8'bz;  // Controlled_Buffer controlled_buffer_2
  assign ram_1_data = and_2_out ? register_2_q : 8'bz;  // Controlled_Buffer controlled_buffer_3
  Clock clock_9 (.out(clock_9_out));
  or or_1 (or_1_out, comparator_4_eq, comparator_5_eq, comparator_7_eq[0]);
  and and_4 (and_4_out, or_1_out, nor_2_out);
  and and_5 (and_5_out, nor_2_out, comparator_7_eq[0], not_3_out);
  assign ram_1_data = and_5_out ? R_IN_q : 8'bz;  // Controlled_Buffer controlled_buffer_4
  not not_4 (not_4_out, clock_9_out);
  monostable monostable_1 (.WAVE(not_4_out), .PULSE(monostable_1_pulse));
  Clock clock_10 (.out(clock_10_out));
  monostable monostable_2 (.WAVE(clock_10_out), .PULSE(monostable_2_pulse));
  or or_2 (or_2_out, comparator_2_eq, comparator_3_eq);
  Clock clock_11 (.out(clock_11_out));
  not not_5 (not_5_out, clock_11_out);
  Clock clock_12 (.out(clock_12_out));
  or or_3 (or_3_out, comparator_8_eq, comparator_9_eq);
  and and_6 (and_6_out, d_ff_1_q, d_ff_2_q);
  not not_6 (not_6_out, OUTPUT_READY);
  monostable monostable_3 (.WAVE(not_5_out), .PULSE(monostable_3_pulse));
  monostable monostable_4 (.WAVE(clock_12_out), .PULSE(monostable_4_pulse));
  Comparator comparator_10 (.a(ram_1_data), .b({8{1'b0}}), .eq(comparator_10_eq));  // open: gt, lt
  not not_7 (not_7_out, comparator_10_eq);
  and and_7 (and_7_out, not_7_out, comparator_9_eq);
  D_Flip_Flop d_ff_1 (.D(and_6_out), .clk(clock_13_out), .Q(d_ff_1_q), .preset(and_8_out));  // open: Qn, reset
  Clock clock_13 (.out(clock_13_out));
  and and_8 (and_8_out, OUTPUT_READY, monostable_1_pulse, comparator_6_eq);
  and and_9 (and_9_out, not_6_out, monostable_1_pulse, comparator_6_eq);
  D_Flip_Flop d_ff_2 (.Q(d_ff_2_q), .preset(and_9_out), .reset(and_10_out));  // open: D, clk, Qn
  and and_10 (and_10_out, OUTPUT_READY, monostable_2_pulse);
  Register #(.trigger("falling")) R_OUT (
    .D(ram_1_data), .en(comparator_6_eq), .clk(clock_14_out), .Q(R_OUT_q));  // open: clr
  Clock clock_14 (.out(clock_14_out));
  Register R_IN (.D(EXT_OUTPUT), .en(comparator_7_eq[0]), .clk(CLK), .Q(R_IN_q));  // open: clr
  D_Flip_Flop #(.trigger("falling")) d_ff_3 (
    .D(and_11_out), .clk(clock_15_out), .Q(d_ff_3_q), .preset(CLK));  // open: Qn, reset
  and and_11 (and_11_out, d_ff_4_q, d_ff_3_q);
  Clock clock_15 (.out(clock_15_out));
  not not_8 (not_8_out, d_ff_3_q);
  and and_12 (and_12_out, comparator_7_eq[0], not_8_out, monostable_3_pulse);
  and and_13 (and_13_out, d_ff_3_q, monostable_4_pulse);
  and and_14 (and_14_out, d_ff_5_q, not_9_out);
  not not_9 (not_9_out, comparator_9_eq);
  and and_15 (and_15_out, comparator_10_eq, comparator_8_eq);
  and and_16 (and_16_out, not_7_out, comparator_8_eq);
  D_Flip_Flop d_ff_4 (.Q(d_ff_4_q), .preset(and_12_out), .reset(and_13_out));  // open: D, clk, Qn
  D_Flip_Flop #(.trigger("falling")) d_ff_5 (
    .D(or_4_out), .clk(clock_16_out), .Q(d_ff_5_q));  // open: Qn, preset, reset
  or or_4 (or_4_out, and_14_out, and_15_out);
  Clock clock_16 (.out(clock_16_out));
  assign EXT_OUTPUT = comparator_6_eq ? R_OUT_q : 8'bz;  // Controlled_Buffer controlled_buffer_5
  assign CLK = comparator_6_eq ? d_ff_1_q : 1'bz;  // Controlled_Buffer controlled_buffer_6
  assign {EXT_OUTPUT, CLK} = comparator_7_eq[0] ? {EXT_INPUT, EXT_CLK_out[0]} : 9'bz;  // Controlled_Buffer controlled_buffer_7
  Button EXT_CLK (.out(EXT_CLK_out[0]));

  // Notes on the sheet:
  //   contents of rom_1 (hex, n*v repeats v):
  //   2b 2b 5b 2d 5d 5b 2d 2b 2d 5d
  //   \0
  //   >
  //   <
  //   +
  //   -
  //   .
  //   ,
  //   [
  //   ]
  //   OE
  //   IE
  //   State OUTPUT
  //   State INPUT
  //   State JUMPING
endmodule

module monostable (
  input  WAVE,
  output PULSE
);

  wire not_1_out;

  not not_1 (not_1_out, WAVE);
  and and_1 (PULSE, not_1_out, WAVE);
endmodule
